# Fritzing sketch ir_sketch (saved by Fritzing 0.8.5b)
circuit board: 5cm x 6cm
breadboards: 1

parts:
  LED = LPD8806 RGB LED Strip
  5V_2A_AC = 2.1mm Barrel Jack with Terminal Block
  PIR1 = PIR sensor
  ATMega328p = MICROCONTROLLER [package=dil28-3-simon-kit]
  VCC1 = Battery block 9V

nets:
  GND: LED.GND, 5V_2A_AC.NEG, PIR1.GND, ATMega328p.GND, VCC1.-
  N1: LED.DI, ATMega328p.PD0(RXD)
  N2: LED.CI, ATMega328p.PD1(TXD)
  N3: LED.+5V, 5V_2A_AC.POS
  VDD: PIR1.VDD, ATMega328p.VCC, VCC1.+
  N4: PIR1.SIG, ATMega328p.PB0(ICP)

notes:
  ci
  di
  GND

custom parts:
  LPD8806 RGB LED Strip: Digitally addressable RGB LED strip
